# Fritzing sketch wiring (saved by Fritzing 0.9.3b)
breadboards: 1

parts:
  Raspberry_Pi_1 = Raspberry Pi 3 [part_number=RPI-3-V1.2]
  PIR1 = PIR sensor
  LED1 = smd LED [color="Red (633nm)" package="0603 [SMD]"]
  LED2 = smd LED [color="Green (555nm)" package="0603 [SMD]"]
  R1 = Resistor [tolerance=±5% resistance=220 package=THT]
  R2 = Resistor [tolerance=±5% resistance=220 package=THT]

nets:
  N1: Raspberry_Pi_1.GIPO4, PIR1.VDD
  N2: Raspberry_Pi_1.GIPO17, LED2.anode
  N3: Raspberry_Pi_1.GIPO18, LED1.anode
  GND: Raspberry_Pi_1.GND, PIR1.GND, R1.Pin_0, R2.Pin_0
  N4: Raspberry_Pi_1.5V, PIR1.SIG
  N5: LED1.cathode, R2.Pin_1
  N6: LED2.cathode, R1.Pin_1
